// Logisim project 32x32-bit-register-file.circ as structural Verilog: 3 circuits, main circuit main
module main (
  input  Clock,
  input  [4:0] RB,
  input  [4:0] RA,
  input  [31:0] BusW,
  input  [4:0] RW,
  input  RegWrite,
  output [31:0] BusB,
  output [31:0] BusA
);

  wire _1_out, _2_out, _3_out, _4_out, _5_out, _6_out, _7_out, _8_out, _9_out, _10_out, _11_out, _12_out,
       _13_out, _14_out, _15_out, _16_out, _17_out, _18_out, _19_out, _20_out, _21_out, _22_out, _23_out,
       _24_out, _25_out, _26_out, _27_out, _28_out, _29_out, _30_out, _31_out, decoder_1_out1,
       decoder_1_out2, decoder_1_out3, decoder_1_out4, decoder_1_out5, decoder_1_out6, decoder_1_out7,
       decoder_1_out8, decoder_1_out9, decoder_1_out10, decoder_1_out11, decoder_1_out12, decoder_1_out13,
       decoder_1_out14, decoder_1_out15, decoder_1_out16, decoder_1_out17, decoder_1_out18, decoder_1_out19,
       decoder_1_out20, decoder_1_out21, decoder_1_out22, decoder_1_out23, decoder_1_out24, decoder_1_out25,
       decoder_1_out26, decoder_1_out27, decoder_1_out28, decoder_1_out29, decoder_1_out30, decoder_1_out31,
       decoder_2_out0, decoder_2_out1, decoder_2_out2, decoder_2_out3, decoder_2_out4, decoder_2_out5,
       decoder_2_out6, decoder_2_out7, decoder_2_out8, decoder_2_out9, decoder_2_out10, decoder_2_out11,
       decoder_2_out12, decoder_2_out13, decoder_2_out14, decoder_2_out15, decoder_2_out16, decoder_2_out17,
       decoder_2_out18, decoder_2_out19, decoder_2_out20, decoder_2_out21, decoder_2_out22, decoder_2_out23,
       decoder_2_out24, decoder_2_out25, decoder_2_out26, decoder_2_out27, decoder_2_out28, decoder_2_out29,
       decoder_2_out30, decoder_2_out31, decoder_3_out0, decoder_3_out1, decoder_3_out2, decoder_3_out3,
       decoder_3_out4, decoder_3_out5, decoder_3_out6, decoder_3_out7, decoder_3_out8, decoder_3_out9,
       decoder_3_out10, decoder_3_out11, decoder_3_out12, decoder_3_out13, decoder_3_out14, decoder_3_out15,
       decoder_3_out16, decoder_3_out17, decoder_3_out18, decoder_3_out19, decoder_3_out20, decoder_3_out21,
       decoder_3_out22, decoder_3_out23, decoder_3_out24, decoder_3_out25, decoder_3_out26, decoder_3_out27,
       decoder_3_out28, decoder_3_out29, decoder_3_out30, decoder_3_out31;
  wire [31:0] R1_q, R2_q, R3_q, R4_q, R5_q, R6_q, R7_q, R8_q, R9_q, R10_q, R11_q, R12_q, R13_q, R14_q, R15_q,
       R16_q, R17_q, R18_q, R19_q, R20_q, R21_q, R22_q, R23_q, R24_q, R25_q, R26_q, R27_q, R28_q, R29_q,
       R30_q, R31_q;

  Decoder #(.select(5)) decoder_1 (
    .out1(decoder_1_out1), .out2(decoder_1_out2), .out3(decoder_1_out3), .out4(decoder_1_out4),
    .out5(decoder_1_out5), .out6(decoder_1_out6), .out7(decoder_1_out7), .out8(decoder_1_out8),
    .out9(decoder_1_out9), .out10(decoder_1_out10), .out11(decoder_1_out11), .out12(decoder_1_out12),
    .out13(decoder_1_out13), .out14(decoder_1_out14), .out15(decoder_1_out15), .out16(decoder_1_out16),
    .out17(decoder_1_out17), .out18(decoder_1_out18), .out19(decoder_1_out19), .out20(decoder_1_out20),
    .out21(decoder_1_out21), .out22(decoder_1_out22), .out23(decoder_1_out23), .out24(decoder_1_out24),
    .out25(decoder_1_out25), .out26(decoder_1_out26), .out27(decoder_1_out27), .out28(decoder_1_out28),
    .out29(decoder_1_out29), .out30(decoder_1_out30), .out31(decoder_1_out31), .sel(RW), .en(1'b1));  // open: out0
  and _25 (_25_out, decoder_1_out25, RegWrite);
  and _26 (_26_out, decoder_1_out26, RegWrite);
  and _27 (_27_out, decoder_1_out27, RegWrite);
  and _28 (_28_out, decoder_1_out28, RegWrite);
  and _29 (_29_out, decoder_1_out29, RegWrite);
  and _30 (_30_out, decoder_1_out30, RegWrite);
  and _31 (_31_out, decoder_1_out31, RegWrite);
  Register #(.width(32)) R25 (.D(BusW), .en(_25_out), .Q(R25_q), .clk(Clock));  // open: clr
  Register #(.width(32)) R26 (.D(BusW), .en(_26_out), .Q(R26_q), .clk(Clock));  // open: clr
  Register #(.width(32)) R27 (.D(BusW), .en(_27_out), .Q(R27_q), .clk(Clock));  // open: clr
  Register #(.width(32)) R28 (.D(BusW), .en(_28_out), .Q(R28_q), .clk(Clock));  // open: clr
  Register #(.width(32)) R29 (.D(BusW), .en(_29_out), .Q(R29_q), .clk(Clock));  // open: clr
  Register #(.width(32)) R30 (.D(BusW), .en(_30_out), .Q(R30_q), .clk(Clock));  // open: clr
  Register #(.width(32)) R31 (.D(BusW), .en(_31_out), .Q(R31_q), .clk(Clock));  // open: clr
  and _17 (_17_out, decoder_1_out17, RegWrite);
  and _18 (_18_out, decoder_1_out18, RegWrite);
  and _19 (_19_out, decoder_1_out19, RegWrite);
  and _20 (_20_out, decoder_1_out20, RegWrite);
  and _21 (_21_out, decoder_1_out21, RegWrite);
  and _22 (_22_out, decoder_1_out22, RegWrite);
  and _23 (_23_out, decoder_1_out23, RegWrite);
  and _24 (_24_out, decoder_1_out24, RegWrite);
  Register #(.width(32)) R17 (.D(BusW), .en(_17_out), .Q(R17_q), .clk(Clock));  // open: clr
  Register #(.width(32)) R18 (.D(BusW), .en(_18_out), .Q(R18_q), .clk(Clock));  // open: clr
  Register #(.width(32)) R19 (.D(BusW), .en(_19_out), .Q(R19_q), .clk(Clock));  // open: clr
  Register #(.width(32)) R20 (.D(BusW), .en(_20_out), .Q(R20_q), .clk(Clock));  // open: clr
  Register #(.width(32)) R21 (.D(BusW), .en(_21_out), .Q(R21_q), .clk(Clock));  // open: clr
  Register #(.width(32)) R22 (.D(BusW), .en(_22_out), .Q(R22_q), .clk(Clock));  // open: clr
  Register #(.width(32)) R23 (.D(BusW), .en(_23_out), .Q(R23_q), .clk(Clock));  // open: clr
  Register #(.width(32)) R24 (.D(BusW), .en(_24_out), .Q(R24_q), .clk(Clock));  // open: clr
  and _9 (_9_out, decoder_1_out9, RegWrite);
  and _10 (_10_out, decoder_1_out10, RegWrite);
  and _11 (_11_out, decoder_1_out11, RegWrite);
  and _12 (_12_out, decoder_1_out12, RegWrite);
  and _13 (_13_out, decoder_1_out13, RegWrite);
  and _14 (_14_out, decoder_1_out14, RegWrite);
  and _15 (_15_out, decoder_1_out15, RegWrite);
  and _16 (_16_out, decoder_1_out16, RegWrite);
  and _1 (_1_out, decoder_1_out1, RegWrite);
  and _2 (_2_out, decoder_1_out2, RegWrite);
  and _3 (_3_out, decoder_1_out3, RegWrite);
  and _4 (_4_out, decoder_1_out4, RegWrite);
  and _5 (_5_out, decoder_1_out5, RegWrite);
  and _6 (_6_out, decoder_1_out6, RegWrite);
  and _7 (_7_out, decoder_1_out7, RegWrite);
  and _8 (_8_out, decoder_1_out8, RegWrite);
  Register #(.width(32)) R9 (.D(BusW), .en(_9_out), .Q(R9_q), .clk(Clock));  // open: clr
  Register #(.width(32)) R10 (.D(BusW), .en(_10_out), .Q(R10_q), .clk(Clock));  // open: clr
  Register #(.width(32)) R11 (.D(BusW), .en(_11_out), .Q(R11_q), .clk(Clock));  // open: clr
  Register #(.width(32)) R12 (.D(BusW), .en(_12_out), .Q(R12_q), .clk(Clock));  // open: clr
  Register #(.width(32)) R13 (.D(BusW), .en(_13_out), .Q(R13_q), .clk(Clock));  // open: clr
  Register #(.width(32)) R14 (.D(BusW), .en(_14_out), .Q(R14_q), .clk(Clock));  // open: clr
  Register #(.width(32)) R15 (.D(BusW), .en(_15_out), .Q(R15_q), .clk(Clock));  // open: clr
  Register #(.width(32)) R16 (.D(BusW), .en(_16_out), .Q(R16_q), .clk(Clock));  // open: clr
  Register #(.width(32)) R1 (.D(BusW), .en(_1_out), .Q(R1_q), .clk(Clock));  // open: clr
  Register #(.width(32)) R2 (.D(BusW), .en(_2_out), .Q(R2_q), .clk(Clock));  // open: clr
  Register #(.width(32)) R3 (.D(BusW), .en(_3_out), .Q(R3_q), .clk(Clock));  // open: clr
  Register #(.width(32)) R4 (.D(BusW), .en(_4_out), .Q(R4_q), .clk(Clock));  // open: clr
  Register #(.width(32)) R5 (.D(BusW), .en(_5_out), .Q(R5_q), .clk(Clock));  // open: clr
  Register #(.width(32)) R6 (.D(BusW), .en(_6_out), .Q(R6_q), .clk(Clock));  // open: clr
  Register #(.width(32)) R7 (.D(BusW), .en(_7_out), .Q(R7_q), .clk(Clock));  // open: clr
  Register #(.width(32)) R8 (.D(BusW), .en(_8_out), .Q(R8_q), .clk(Clock));  // open: clr
  assign BusA = decoder_2_out0 ? {32{1'b0}} : 32'bz;  // Controlled_Buffer controlled_buffer_1
  assign BusA = decoder_2_out3 ? R3_q : 32'bz;  // Controlled_Buffer controlled_buffer_2
  assign BusA = decoder_2_out2 ? R2_q : 32'bz;  // Controlled_Buffer controlled_buffer_3
  assign BusA = decoder_2_out1 ? R1_q : 32'bz;  // Controlled_Buffer controlled_buffer_4
  assign BusA = decoder_2_out7 ? R7_q : 32'bz;  // Controlled_Buffer controlled_buffer_5
  assign BusA = decoder_2_out6 ? R6_q : 32'bz;  // Controlled_Buffer controlled_buffer_6
  assign BusA = decoder_2_out5 ? R5_q : 32'bz;  // Controlled_Buffer controlled_buffer_7
  assign BusA = decoder_2_out4 ? R4_q : 32'bz;  // Controlled_Buffer controlled_buffer_8
  assign BusA = decoder_2_out11 ? R11_q : 32'bz;  // Controlled_Buffer controlled_buffer_9
  assign BusA = decoder_2_out10 ? R10_q : 32'bz;  // Controlled_Buffer controlled_buffer_10
  assign BusA = decoder_2_out9 ? R9_q : 32'bz;  // Controlled_Buffer controlled_buffer_11
  assign BusA = decoder_2_out8 ? R8_q : 32'bz;  // Controlled_Buffer controlled_buffer_12
  assign BusA = decoder_2_out15 ? R15_q : 32'bz;  // Controlled_Buffer controlled_buffer_13
  assign BusA = decoder_2_out14 ? R14_q : 32'bz;  // Controlled_Buffer controlled_buffer_14
  assign BusA = decoder_2_out13 ? R13_q : 32'bz;  // Controlled_Buffer controlled_buffer_15
  assign BusA = decoder_2_out12 ? R12_q : 32'bz;  // Controlled_Buffer controlled_buffer_16
  Decoder #(.select(5)) decoder_2 (
    .out0(decoder_2_out0), .out1(decoder_2_out1), .out2(decoder_2_out2), .out3(decoder_2_out3),
    .out4(decoder_2_out4), .out5(decoder_2_out5), .out6(decoder_2_out6), .out7(decoder_2_out7),
    .out8(decoder_2_out8), .out9(decoder_2_out9), .out10(decoder_2_out10), .out11(decoder_2_out11),
    .out12(decoder_2_out12), .out13(decoder_2_out13), .out14(decoder_2_out14), .out15(decoder_2_out15),
    .out16(decoder_2_out16), .out17(decoder_2_out17), .out18(decoder_2_out18), .out19(decoder_2_out19),
    .out20(decoder_2_out20), .out21(decoder_2_out21), .out22(decoder_2_out22), .out23(decoder_2_out23),
    .out24(decoder_2_out24), .out25(decoder_2_out25), .out26(decoder_2_out26), .out27(decoder_2_out27),
    .out28(decoder_2_out28), .out29(decoder_2_out29), .out30(decoder_2_out30), .out31(decoder_2_out31),
    .sel(RA), .en(1'b1));
  assign BusA = decoder_2_out19 ? R19_q : 32'bz;  // Controlled_Buffer controlled_buffer_17
  assign BusA = decoder_2_out18 ? R18_q : 32'bz;  // Controlled_Buffer controlled_buffer_18
  assign BusA = decoder_2_out17 ? R17_q : 32'bz;  // Controlled_Buffer controlled_buffer_19
  assign BusA = decoder_2_out16 ? R16_q : 32'bz;  // Controlled_Buffer controlled_buffer_20
  assign BusA = decoder_2_out23 ? R23_q : 32'bz;  // Controlled_Buffer controlled_buffer_21
  assign BusA = decoder_2_out22 ? R22_q : 32'bz;  // Controlled_Buffer controlled_buffer_22
  assign BusA = decoder_2_out21 ? R21_q : 32'bz;  // Controlled_Buffer controlled_buffer_23
  assign BusA = decoder_2_out20 ? R20_q : 32'bz;  // Controlled_Buffer controlled_buffer_24
  assign BusA = decoder_2_out27 ? R27_q : 32'bz;  // Controlled_Buffer controlled_buffer_25
  assign BusA = decoder_2_out26 ? R26_q : 32'bz;  // Controlled_Buffer controlled_buffer_26
  assign BusA = decoder_2_out25 ? R25_q : 32'bz;  // Controlled_Buffer controlled_buffer_27
  assign BusA = decoder_2_out24 ? R24_q : 32'bz;  // Controlled_Buffer controlled_buffer_28
  assign BusA = decoder_2_out31 ? R31_q : 32'bz;  // Controlled_Buffer controlled_buffer_29
  assign BusA = decoder_2_out30 ? R30_q : 32'bz;  // Controlled_Buffer controlled_buffer_30
  assign BusA = decoder_2_out29 ? R29_q : 32'bz;  // Controlled_Buffer controlled_buffer_31
  assign BusA = decoder_2_out28 ? R28_q : 32'bz;  // Controlled_Buffer controlled_buffer_32
  assign BusB = decoder_3_out0 ? {32{1'b0}} : 32'bz;  // Controlled_Buffer controlled_buffer_33
  assign BusB = decoder_3_out1 ? R1_q : 32'bz;  // Controlled_Buffer controlled_buffer_34
  assign BusB = decoder_3_out5 ? R5_q : 32'bz;  // Controlled_Buffer controlled_buffer_35
  assign BusB = decoder_3_out4 ? R4_q : 32'bz;  // Controlled_Buffer controlled_buffer_36
  assign BusB = decoder_3_out3 ? R3_q : 32'bz;  // Controlled_Buffer controlled_buffer_37
  assign BusB = decoder_3_out2 ? R2_q : 32'bz;  // Controlled_Buffer controlled_buffer_38
  assign BusB = decoder_3_out9 ? R9_q : 32'bz;  // Controlled_Buffer controlled_buffer_39
  assign BusB = decoder_3_out8 ? R8_q : 32'bz;  // Controlled_Buffer controlled_buffer_40
  assign BusB = decoder_3_out7 ? R7_q : 32'bz;  // Controlled_Buffer controlled_buffer_41
  assign BusB = decoder_3_out6 ? R6_q : 32'bz;  // Controlled_Buffer controlled_buffer_42
  assign BusB = decoder_3_out13 ? R13_q : 32'bz;  // Controlled_Buffer controlled_buffer_43
  assign BusB = decoder_3_out12 ? R12_q : 32'bz;  // Controlled_Buffer controlled_buffer_44
  assign BusB = decoder_3_out11 ? R11_q : 32'bz;  // Controlled_Buffer controlled_buffer_45
  assign BusB = decoder_3_out10 ? R10_q : 32'bz;  // Controlled_Buffer controlled_buffer_46
  assign BusB = decoder_3_out17 ? R17_q : 32'bz;  // Controlled_Buffer controlled_buffer_47
  assign BusB = decoder_3_out16 ? R16_q : 32'bz;  // Controlled_Buffer controlled_buffer_48
  assign BusB = decoder_3_out15 ? R15_q : 32'bz;  // Controlled_Buffer controlled_buffer_49
  assign BusB = decoder_3_out14 ? R14_q : 32'bz;  // Controlled_Buffer controlled_buffer_50
  Decoder #(.select(5)) decoder_3 (
    .out0(decoder_3_out0), .out1(decoder_3_out1), .out2(decoder_3_out2), .out3(decoder_3_out3),
    .out4(decoder_3_out4), .out5(decoder_3_out5), .out6(decoder_3_out6), .out7(decoder_3_out7),
    .out8(decoder_3_out8), .out9(decoder_3_out9), .out10(decoder_3_out10), .out11(decoder_3_out11),
    .out12(decoder_3_out12), .out13(decoder_3_out13), .out14(decoder_3_out14), .out15(decoder_3_out15),
    .out16(decoder_3_out16), .out17(decoder_3_out17), .out18(decoder_3_out18), .out19(decoder_3_out19),
    .out20(decoder_3_out20), .out21(decoder_3_out21), .out22(decoder_3_out22), .out23(decoder_3_out23),
    .out24(decoder_3_out24), .out25(decoder_3_out25), .out26(decoder_3_out26), .out27(decoder_3_out27),
    .out28(decoder_3_out28), .out29(decoder_3_out29), .out30(decoder_3_out30), .out31(decoder_3_out31),
    .sel(RB), .en(1'b1));
  assign BusB = decoder_3_out21 ? R21_q : 32'bz;  // Controlled_Buffer controlled_buffer_51
  assign BusB = decoder_3_out20 ? R20_q : 32'bz;  // Controlled_Buffer controlled_buffer_52
  assign BusB = decoder_3_out19 ? R19_q : 32'bz;  // Controlled_Buffer controlled_buffer_53
  assign BusB = decoder_3_out18 ? R18_q : 32'bz;  // Controlled_Buffer controlled_buffer_54
  assign BusB = decoder_3_out25 ? R25_q : 32'bz;  // Controlled_Buffer controlled_buffer_55
  assign BusB = decoder_3_out24 ? R24_q : 32'bz;  // Controlled_Buffer controlled_buffer_56
  assign BusB = decoder_3_out23 ? R23_q : 32'bz;  // Controlled_Buffer controlled_buffer_57
  assign BusB = decoder_3_out22 ? R22_q : 32'bz;  // Controlled_Buffer controlled_buffer_58
  assign BusB = decoder_3_out29 ? R29_q : 32'bz;  // Controlled_Buffer controlled_buffer_59
  assign BusB = decoder_3_out28 ? R28_q : 32'bz;  // Controlled_Buffer controlled_buffer_60
  assign BusB = decoder_3_out27 ? R27_q : 32'bz;  // Controlled_Buffer controlled_buffer_61
  assign BusB = decoder_3_out26 ? R26_q : 32'bz;  // Controlled_Buffer controlled_buffer_62
  assign BusB = decoder_3_out31 ? R31_q : 32'bz;  // Controlled_Buffer controlled_buffer_63
  assign BusB = decoder_3_out30 ? R30_q : 32'bz;  // Controlled_Buffer controlled_buffer_64

  // Notes on the sheet:
  //   STAGE 1
  //   STAGE 2
endmodule

module Stage2 (
  input  [4:0] RA,
  input  [4:0] RB,
  input  [4:0] RW,
  input  [31:0] BusW,
  input  Enable_Write,
  input  Arith_Selection,
  input  [1:0] Shift_Rotate_Selection,
  input  [1:0] Logical_Operation_Selector,
  input  [1:0] ALU_Selection,
  input  Enable,
  output [31:0] BusA,
  output [31:0] BusB,
  output [31:0] out_13
);

  wire clock_1_out;
  wire [31:0] n32bit_alu_1_alu_result;

  Clock clock_1 (.out(clock_1_out));
  main main_1 (
    .BusW(BusW), .RegWrite(Enable_Write), .RA(RA), .RB(RB), .Clock(clock_1_out), .RW(RW), .BusA(BusA),
    .BusB(BusB));
  _32bit_ALU u_32bit_alu_1 (
    .A(BusA), .B(BusB), .Arith_Selection(Arith_Selection), .Shift_Rotate_Selection(Shift_Rotate_Selection),
    .Logical_Op_Selection(Logical_Operation_Selector), .ALU_Selection(ALU_Selection),
    .ALU_Result(n32bit_alu_1_alu_result), .Enable(Enable));
  Register #(.width(32)) register_1 (
    .D(n32bit_alu_1_alu_result), .en(Enable), .Q(out_13), .clk(clock_1_out));  // open: clr

  // Notes on the sheet:
  //   Testing Registar-File + ALU
endmodule

module _32bit_ALU (
  input  [1:0] Shift_Rotate_Selection,
  input  [31:0] A,
  input  [31:0] B,
  input  Enable,
  input  [1:0] ALU_Selection,
  input  Arith_Selection,
  input  [1:0] Logical_Op_Selection,
  output [31:0] ALU_Result
);

  wire adder_1_cout, and_1_out, bitselector_2_out, bitselector_3_out, bitselector_4_out, not_1_out, or_1_out,
       or_3_out;
  wire [4:0] bitselector_1_out;
  wire [31:0] adder_1_out, and_2_out, and_3_out, bit_extender_1_out, bit_extender_2_out, multiplexer_1_out,
       multiplexer_2_out, not_2_out, or_2_out, shifter_1_out, shifter_2_out, shifter_3_out, shifter_4_out,
       xor_1_out, xor_2_out;

  BitSelector #(.width(32), .group(5)) bitselector_1 (.in(A), .out(bitselector_1_out), .sel(3'b000));
  BitSelector #(.width(2)) bitselector_2 (.in(ALU_Selection), .out(bitselector_2_out), .sel(1'b1));
  BitSelector #(.width(2)) bitselector_3 (.in(ALU_Selection), .out(bitselector_3_out), .sel(1'b0));
  and and_1 (and_1_out, not_1_out, bitselector_3_out);
  not not_1 (not_1_out, bitselector_2_out);
  or or_1 (or_1_out, Arith_Selection, and_1_out);
  assign bit_extender_1_out = {{31{1'b0}}, or_1_out};  // Bit_Extender bit_extender_1
  Shifter #(.width(32)) shifter_1 (.in(B), .\dist (bitselector_1_out), .out(shifter_1_out));
  Shifter #(.width(32), .shift("ar")) shifter_2 (.in(B), .\dist (bitselector_1_out), .out(shifter_2_out));
  assign xor_1_out = B ^ bit_extender_1_out;  // XOR_Gate xor_1, 32 bits wide
  assign and_2_out = A & B;  // AND_Gate and_2, 32 bits wide
  assign or_2_out = A | B;  // OR_Gate or_2, 32 bits wide
  assign xor_2_out = A ^ B;  // XOR_Gate xor_2, 32 bits wide
  Shifter #(.width(32), .shift("lr")) shifter_3 (.in(B), .\dist (bitselector_1_out), .out(shifter_3_out));
  Shifter #(.width(32), .shift("rr")) shifter_4 (.in(B), .\dist (bitselector_1_out), .out(shifter_4_out));
  assign not_2_out = ~or_2_out;  // NOT_Gate not_2, 32 bits wide
  Multiplexer #(.select(2), .width(32)) multiplexer_1 (
    .in0(shifter_1_out), .in1(shifter_3_out), .in2(shifter_2_out), .in3(shifter_4_out),
    .out(multiplexer_1_out), .sel(Shift_Rotate_Selection), .en(1'b1));
  assign and_3_out = 32'h80000000 & adder_1_out;  // AND_Gate and_3, 32 bits wide
  Multiplexer #(.select(2), .width(32)) multiplexer_2 (
    .in0(and_2_out), .in1(or_2_out), .in2(not_2_out), .in3(xor_2_out), .out(multiplexer_2_out),
    .sel(Logical_Op_Selection), .en(1'b1));
  BitSelector #(.width(32)) bitselector_4 (.in(and_3_out), .out(bitselector_4_out), .sel({5{1'b1}}));
  or or_3 (or_3_out, bitselector_4_out, adder_1_cout);
  Adder #(.width(32)) adder_1 (.a(A), .b(xor_1_out), .out(adder_1_out), .cin(or_1_out), .cout(adder_1_cout));
  assign bit_extender_2_out = {{31{1'b0}}, or_3_out};  // Bit_Extender bit_extender_2
  Multiplexer #(.select(2), .width(32)) multiplexer_3 (
    .in0(multiplexer_1_out), .in1(bit_extender_2_out), .in2(adder_1_out), .in3(multiplexer_2_out),
    .out(ALU_Result), .sel(ALU_Selection), .en(Enable));
endmodule
