// Logisim project Pipelined Processor Design.circ as structural Verilog: 3 circuits, main circuit main
module main (
  output [15:0] out_1
);

  wire addi, AluSrc, and_5_out, and_6_out, and_7_out, and_9_out, and_10_out, and_11_out, and_12_out,
       and_13_out, and_14_out, and_16_out, and_17_out, and_18_out, and_19_out, and_20_out, and_21_out,
       and_22_out, and_24_out, and_25_out, and_26_out, and_27_out, and_28_out, and_29_out, and_30_out,
       and_31_out, and_32_out, andi, Branch, Clk, comparator_1_eq, comparator_2_eq, comparator_3_eq,
       comparator_4_eq, comparator_5_eq, comparator_6_eq, comparator_7_eq, comparator_8_eq, comparator_9_gt,
       controlled_buffer_1_out, controlled_buffer_2_out, controlled_buffer_3_out, controlled_buffer_4_out,
       controlled_buffer_5_out, controlled_buffer_6_out, decoder_1_out1, j, j_br, jal, jal_br, JALR, JALR_br,
       JR, JR_br, Kill1, lui, LW, lw_t, multiplexer_11_out, multiplexer_14_out, multiplexer_20_out,
       multiplexer_22_out, not_1_out, not_2_out, not_3_out, not_4_out, not_5_out, not_6_out, not_7_out,
       not_8_out, not_9_out, not_10_out, not_11_out, not_12_out, not_13_out, not_14_out, not_15_out,
       not_16_out, not_17_out, not_18_out, not_19_out, not_20_out, not_21_out, not_22_out, not_23_out,
       not_24_out, or_1_out, or_5_out, or_6_out, or_7_out, or_8_out, or_9_out, or_10_out, or_11_out,
       or_13_out, or_14_out, or_15_out, or_16_out, or_17_out, or_18_out, or_21_out, ori, Rd2_2_q, RegWrite,
       RegWriteEXE, RegWriteMEM, Stall, SW, sw_t, Zero;
  wire [1:0] ForwardA, ForwardB, MemExe, multiplexer_10_out, multiplexer_13_out, multiplexer_15_out,
       multiplexer_17_out, multiplexer_24_out, multiplexer_25_out, or_4_out, or_19_out, WBexe, WBmem;
  wire [2:0] AluSrc_q, Func, multiplexer_3_out, multiplexer_4_out, Rd2, Rd2_q, Rd3, Rd4, RtReal;
  wire [3:0] AluOpCode, multiplexer_21_out, OpCode;
  wire [5:0] Branch_Instructions, Branch_Instructions_Pre, multiplexer_23_out;
  wire [11:0] adder_2_out, Branch_PC, multiplexer_1_out, NPC, NPCAlu, NPCReg, PC, PC_1, Sign_Extended12;
  wire [11:3] J_12Im;
  wire [15:0] AluForward, bit_extender_4_out, BusW, DataForward, DataMemory_Out, Imm, multiplexer_2_out,
       multiplexer_6_out, multiplexer_8_out, multiplexer_19_out, ram_1_data, registerfile_1_busa,
       registerfile_1_busb, Rs_Out, Rs_Out_Need, Rt_Out, Rt_Out_Data, Sign_Extended, Zero_Extended;

  Clock clock_1 (.out(Clk));
  not not_1 (not_1_out, Branch);
  not not_2 (not_2_out, Branch);
  not not_3 (not_3_out, or_1_out);
  not not_4 (not_4_out, Branch);
  not not_5 (not_5_out, or_1_out);
  not not_6 (not_6_out, Branch);
  and and_1 (jal_br, not_1_out, jal);
  and and_2 (j_br, not_2_out, j);
  and and_3 (JR_br, not_3_out, not_4_out, JR);
  and and_4 (JALR_br, not_5_out, not_6_out, JALR);
  or or_1 (or_1_out, jal_br, j_br);
  or or_2 (Kill1, Branch, or_1_out, JR_br, JALR_br);
  Adder #(.width(12)) adder_1 (.a(PC), .b(12'h1), .out(PC_1));  // open: cin, cout
  Multiplexer #(.select(2), .width(12), .enable("false")) multiplexer_1 (
    .in0(PC_1), .in1(Rs_Out_Need[11:0]), .in2(Branch_PC), .in3({J_12Im, Func}), .out(multiplexer_1_out),
    .sel(or_4_out));
  or or_3 (or_4_out[1], or_6_out, Branch);
  or or_4 (or_4_out[0], or_5_out, or_6_out);
  or or_5 (or_5_out, JR_br, JALR_br);
  Register #(.width(12)) u_NPC (.D(PC_1), .en(1'b1), .Q(NPC), .clk(Clk));  // open: clr
  Register #(.width(12)) u_PC (.D(multiplexer_1_out), .en(not_7_out), .Q(PC), .clk(Clk));  // open: clr
  not not_7 (not_7_out, Stall);
  or or_6 (or_6_out, j_br, jal_br);
  RAM #(.addrWidth(12), .dataWidth(16)) ram_1 (.addr(PC), .data(ram_1_data), .clk(Clk));  // open: sel, ld, clr
  Multiplexer #(.width(16), .enable("false")) multiplexer_2 (
    .in0(ram_1_data), .in1({16{1'b0}}), .out(multiplexer_2_out), .sel(Kill1));
  LED led_1 (.in(Kill1));
  LED led_2 (.in(Branch));
  and and_5 (and_5_out, ForwardA[0], not_8_out);
  not not_8 (not_8_out, ForwardA[1]);
  and and_6 (and_6_out, ForwardB[0], not_9_out);
  not not_9 (not_9_out, ForwardB[1]);
  assign Sign_Extended = {{10{J_12Im[5]}}, {J_12Im[5:3], Func}};  // Bit_Extender bit_extender_1
  assign Zero_Extended = {{10{1'b0}}, {J_12Im[5:3], Func}};  // Bit_Extender bit_extender_2
  assign Sign_Extended12 = {{6{J_12Im[5]}}, {J_12Im[5:3], Func}};  // Bit_Extender bit_extender_3
  Register #(.width(16)) Inst (
    .D(multiplexer_2_out), .en(not_10_out), .Q({OpCode, J_12Im, Func}), .clk(Clk));  // open: clr
  not not_10 (not_10_out, Stall);
  and and_7 (and_7_out, MemExe[1], 1'b1);
  or or_7 (or_7_out, and_5_out, and_6_out);
  and and_8 (Stall, and_7_out, or_7_out);
  or or_8 (or_8_out, Branch_Instructions_Pre[0], Branch_Instructions_Pre[1], Branch_Instructions_Pre[2], Branch_Instructions_Pre[3], Branch_Instructions_Pre[4], Branch_Instructions_Pre[5], sw_t);
  Multiplexer #(.width(3), .enable("false")) multiplexer_3 (
    .in0(J_12Im[11:9]), .in1(multiplexer_4_out), .out(multiplexer_3_out), .sel(or_9_out));
  Multiplexer #(.width(3), .enable("false")) multiplexer_4 (
    .in0(3'b111), .in1(3'b001), .out(multiplexer_4_out), .sel(lui));
  or or_9 (or_9_out, jal, lui);
  Multiplexer #(.width(3), .enable("false")) multiplexer_5 (
    .in0(J_12Im[5:3]), .in1(multiplexer_3_out), .out(RtReal), .sel(or_8_out));
  and and_9 (and_9_out, Rd2_q[2], not_11_out, Rd2_q[0]);
  not not_11 (not_11_out, Rd2_q[1]);
  Register #(.width(3)) u_Rd2 (.D(Func), .en(1'b1), .Q(Rd2_q), .clk(Clk));  // open: clr
  or or_10 (or_10_out, addi, sw_t, lw_t);
  RegisterFile registerfile_1 (
    .BusW(BusW), .Clock(Clk), .RegWrite(RegWrite), .RA(J_12Im[8:6]), .RB(RtReal), .RW(Rd4),
    .BusA(registerfile_1_busa), .BusB(registerfile_1_busb));
  Comparator #(.width(3), .mode("unsigned")) comparator_1 (.a(RtReal), .b(Rd2), .eq(comparator_1_eq));  // open: gt, lt
  Comparator #(.width(3), .mode("unsigned")) comparator_2 (.a(RtReal), .b(Rd3), .eq(comparator_2_eq));  // open: gt, lt
  Comparator #(.width(3), .mode("unsigned")) comparator_3 (.a(RtReal), .b(Rd4), .eq(comparator_3_eq));  // open: gt, lt
  and and_10 (and_10_out, and_13_out, Zero);
  and and_11 (and_11_out, and_12_out, not_12_out);
  not not_12 (not_12_out, Zero);
  and and_12 (and_12_out, and_14_out, Rd2_2_q);
  and and_13 (and_13_out, and_9_out, Rd2_2_q);
  and and_14 (and_14_out, Rd2_q[2], not_13_out, not_14_out);
  not not_13 (not_13_out, Rd2_q[1]);
  not not_14 (not_14_out, Rd2_q[0]);
  Multiplexer #(.width(16), .enable("false")) multiplexer_6 (
    .in0(Zero_Extended), .in1(Sign_Extended), .out(multiplexer_6_out), .sel(or_10_out));
  Comparator #(.width(3), .mode("unsigned")) comparator_4 (
    .a(J_12Im[8:6]), .b(Rd2), .eq(comparator_4_eq));  // open: gt, lt
  Comparator #(.width(3), .mode("unsigned")) comparator_5 (
    .a(J_12Im[8:6]), .b(Rd3), .eq(comparator_5_eq));  // open: gt, lt
  Comparator #(.width(3), .mode("unsigned")) comparator_6 (
    .a(J_12Im[8:6]), .b(Rd4), .eq(comparator_6_eq));  // open: gt, lt
  and and_15 (JR, and_16_out, decoder_1_out1);
  and and_16 (and_16_out, Func[2], Func[1], not_15_out);
  not not_15 (not_15_out, Func[0]);
  Register #(.width(1)) Rd2_2 (.D(decoder_1_out1), .en(1'b1), .Q(Rd2_2_q), .clk(Clk));  // open: clr
  Adder #(.width(12)) adder_2 (.a(Sign_Extended12), .b(PC), .out(adder_2_out));  // open: cin, cout
  Register #(.width(12)) BTA (.D(adder_2_out), .en(1'b1), .Q(Branch_PC), .clk(Clk));  // open: clr
  Register #(.width(16)) u_Imm (.D(multiplexer_6_out), .en(1'b1), .Q(Imm), .clk(Clk));  // open: clr
  Register #(.width(3)) Rd2_3 (.D(multiplexer_3_out), .en(1'b1), .Q(Rd2), .clk(Clk));  // open: clr
  and and_17 (and_17_out, comparator_4_eq, RegWriteEXE);
  and and_18 (and_18_out, comparator_5_eq, RegWriteMEM);
  and and_19 (and_19_out, comparator_6_eq, RegWrite);
  and and_20 (and_20_out, comparator_1_eq, RegWriteEXE);
  and and_21 (and_21_out, comparator_2_eq, RegWriteMEM);
  and and_22 (and_22_out, comparator_3_eq, RegWrite);
  and and_23 (JALR, and_24_out, decoder_1_out1);
  and and_24 (and_24_out, Func[2], Func[1], Func[0]);
  Comparator #(.width(3), .mode("unsigned")) comparator_7 (
    .a(J_12Im[8:6]), .b(3'b000), .eq(comparator_7_eq));  // open: gt, lt
  not not_16 (not_16_out, and_17_out);
  assign controlled_buffer_1_out = not_16_out ? and_18_out : 1'bz;  // Controlled_Buffer controlled_buffer_1
  not not_17 (not_17_out, and_18_out);
  assign controlled_buffer_2_out = not_17_out ? and_19_out : 1'bz;  // Controlled_Buffer controlled_buffer_2
  Comparator #(.width(3), .mode("unsigned")) comparator_8 (
    .a(RtReal), .b(3'b000), .eq(comparator_8_eq));  // open: gt, lt
  not not_18 (not_18_out, and_20_out);
  assign controlled_buffer_3_out = not_18_out ? and_21_out : 1'bz;  // Controlled_Buffer controlled_buffer_3
  not not_19 (not_19_out, and_21_out);
  assign controlled_buffer_4_out = not_19_out ? and_22_out : 1'bz;  // Controlled_Buffer controlled_buffer_4
  assign controlled_buffer_5_out = not_18_out ? controlled_buffer_4_out : 1'bz;  // Controlled_Buffer controlled_buffer_5
  Register #(.width(16)) A (.D(Rs_Out_Need), .en(1'b1), .Q(Rs_Out), .clk(Clk));  // open: clr
  Multiplexer #(.select(2), .width(16), .enable("false")) multiplexer_7 (
    .in0(registerfile_1_busa), .in1(AluForward), .in2(DataForward), .in3(BusW), .out(Rs_Out_Need),
    .sel(ForwardA));
  Multiplexer #(.select(2), .width(16), .enable("false")) multiplexer_8 (
    .in0(registerfile_1_busb), .in1(AluForward), .in2(DataForward), .in3(BusW), .out(multiplexer_8_out),
    .sel(ForwardB));
  Register #(.width(16)) B (.D(multiplexer_8_out), .en(1'b1), .Q(Rt_Out), .clk(Clk));  // open: clr
  Multiplexer #(.select(2), .width(2), .enable("false")) multiplexer_9 (
    .in0(2'b00), .in1(2'b01), .in2(2'b10), .in3(2'b11), .out(ForwardA), .sel(multiplexer_10_out));
  Multiplexer #(.width(2), .enable("false")) multiplexer_10 (
    .in0(multiplexer_15_out), .in1(2'b00), .out(multiplexer_10_out), .sel(comparator_7_eq));
  Multiplexer #(.enable("false")) multiplexer_11 (
    .in0(controlled_buffer_1_out), .in1(controlled_buffer_6_out), .out(multiplexer_11_out), .sel(and_25_out));
  assign controlled_buffer_6_out = not_16_out ? controlled_buffer_2_out : 1'bz;  // Controlled_Buffer controlled_buffer_6
  and and_25 (and_25_out, not_21_out, not_20_out);
  not not_20 (not_20_out, and_18_out);
  not not_21 (not_21_out, and_17_out);
  Multiplexer #(.select(2), .width(2), .enable("false")) multiplexer_12 (
    .in0(2'b00), .in1(2'b01), .in2(2'b10), .in3(2'b11), .out(ForwardB), .sel(multiplexer_13_out));
  Multiplexer #(.width(2), .enable("false")) multiplexer_13 (
    .in0(multiplexer_17_out), .in1(2'b00), .out(multiplexer_13_out), .sel(comparator_8_eq));
  Multiplexer #(.enable("false")) multiplexer_14 (
    .in0(controlled_buffer_3_out), .in1(controlled_buffer_5_out), .out(multiplexer_14_out), .sel(and_26_out));
  and and_26 (and_26_out, not_22_out, not_23_out);
  not not_22 (not_22_out, and_20_out);
  not not_23 (not_23_out, and_21_out);
  Decoder #(.select(4), .enable("false")) decoder_1 (
    .out1(decoder_1_out1), .out2(andi), .out3(ori), .out4(addi), .out5(sw_t), .out6(lw_t),
    .out7(Branch_Instructions_Pre[0]), .out8(Branch_Instructions_Pre[1]), .out9(Branch_Instructions_Pre[2]),
    .out10(Branch_Instructions_Pre[3]), .out11(Branch_Instructions_Pre[4]),
    .out12(Branch_Instructions_Pre[5]), .out13(lui), .out14(j), .out15(jal), .sel(OpCode));  // open: out0
  Register #(.width(12)) Rd2_4 (.D(NPC), .en(1'b1), .Q(NPCReg), .clk(Clk));  // open: clr
  Multiplexer #(.enable("false")) multiplexer_15 (
    .in0(and_17_out), .in1(controlled_buffer_6_out), .out(multiplexer_15_out[0]), .sel(and_25_out));
  Multiplexer #(.enable("false")) multiplexer_16 (
    .in0(multiplexer_11_out), .in1(1'b0), .out(multiplexer_15_out[1]), .sel(and_17_out));
  Multiplexer #(.enable("false")) multiplexer_17 (
    .in0(and_20_out), .in1(controlled_buffer_5_out), .out(multiplexer_17_out[0]), .sel(and_26_out));
  Multiplexer #(.enable("false")) multiplexer_18 (
    .in0(multiplexer_14_out), .in1(1'b0), .out(multiplexer_17_out[1]), .sel(and_20_out));
  or or_11 (or_11_out, JR, and_10_out, not_24_out, and_11_out);
  not not_24 (not_24_out, comparator_9_gt);
  Comparator #(.width(11), .mode("unsigned")) comparator_9 (
    .a({1'b0, j, 1'b0, Branch_Instructions_Pre, 1'b0, sw_t}), .b({11{1'b0}}), .gt(comparator_9_gt));  // open: eq, lt
  Multiplexer #(.width(16), .enable("false")) multiplexer_19 (
    .in0(Rt_Out), .in1(Imm), .out(multiplexer_19_out), .sel(AluSrc));
  Register #(.width(3)) u_AluSrc (.D(Func), .en(1'b1), .Q(AluSrc_q), .clk(Clk));  // open: clr
  and and_27 (and_27_out, Branch_Instructions[5], AluForward[0]);
  ALU alu_1 (.Op(AluOpCode), .func(AluSrc_q), .Rt(multiplexer_19_out), .Rs(Rs_Out), .Rd(AluForward), .Zero(Zero));
  Register #(.width(3)) u_Rd3 (.D(Rd2), .en(1'b1), .Q(Rd3), .clk(Clk));  // open: clr
  or or_12 (Branch, and_27_out, and_29_out, and_28_out, and_31_out, and_30_out, and_32_out);
  and and_28 (and_28_out, Branch_Instructions[3], AluForward[0]);
  and and_29 (and_29_out, Branch_Instructions[4], AluForward[0]);
  Multiplexer #(.enable("false")) multiplexer_20 (
    .in0(or_11_out), .in1(1'b0), .out(multiplexer_20_out), .sel(or_13_out));
  or or_13 (or_13_out, Branch, Stall);
  or or_14 (or_14_out, andi, ori, addi, sw_t, lw_t);
  Register #(.width(16)) BTA_2 (.D(AluForward), .en(1'b1), .Q(out_1), .clk(Clk));  // open: clr
  Register #(.width(16)) BTA_3 (.D(Rt_Out), .en(1'b1), .Q(Rt_Out_Data), .clk(Clk));  // open: clr
  and and_30 (and_30_out, Branch_Instructions[1], AluForward[0]);
  and and_31 (and_31_out, Branch_Instructions[2], AluForward[0]);
  Register #(.width(1)) Rd2_5 (.D(multiplexer_20_out), .en(1'b1), .Q(RegWriteEXE), .clk(Clk));  // open: clr
  or or_15 (or_15_out, Branch, Stall);
  Register #(.width(12)) Rd2_6 (.D(NPCReg), .en(1'b1), .Q(NPCAlu), .clk(Clk));  // open: clr
  and and_32 (and_32_out, Branch_Instructions[0], AluForward[0]);
  Multiplexer #(.width(4), .enable("false")) multiplexer_21 (
    .in0(OpCode), .in1(4'b0000), .out(multiplexer_21_out), .sel(or_15_out));
  Multiplexer #(.enable("false")) multiplexer_22 (
    .in0(or_14_out), .in1(1'b0), .out(multiplexer_22_out), .sel(or_16_out));
  or or_16 (or_16_out, Branch, Stall);
  Register #(.width(1)) Rd2_7 (.D(RegWriteEXE), .en(1'b1), .Q(RegWriteMEM), .clk(Clk));  // open: clr
  Register #(.width(4)) u_AluOpCode (.D(multiplexer_21_out), .en(1'b1), .Q(AluOpCode), .clk(Clk));  // open: clr
  Register #(.width(1)) AluSrc_2 (.D(multiplexer_22_out), .en(1'b1), .Q(AluSrc), .clk(Clk));  // open: clr
  Register #(.width(1)) Rd2_8 (.D(RegWriteMEM), .en(1'b1), .Q(RegWrite), .clk(Clk));  // open: clr
  Multiplexer #(.width(6), .enable("false")) multiplexer_23 (
    .in0(Branch_Instructions_Pre), .in1({6{1'b0}}), .out(multiplexer_23_out), .sel(or_17_out));
  or or_17 (or_17_out, Branch, Stall);
  Multiplexer #(.width(2), .enable("false")) multiplexer_24 (
    .in0({lw_t, sw_t}), .in1(2'b00), .out(multiplexer_24_out), .sel(or_18_out));
  or or_18 (or_18_out, Branch, Stall);
  or or_19 (or_19_out[0], JALR, jal, lui);
  or or_20 (or_19_out[1], lw_t, lui);
  Register #(.width(2)) MemExeCU (.D(multiplexer_24_out), .en(1'b1), .Q(MemExe), .clk(Clk));  // open: clr
  Register #(.width(6)) u_Branch_Instructions (
    .D(multiplexer_23_out), .en(1'b1), .Q(Branch_Instructions), .clk(Clk));  // open: clr
  Register #(.width(16)) Data (.D(DataForward), .en(1'b1), .Q(BusW), .clk(Clk));  // open: clr
  Register #(.width(3)) u_Rd4 (.D(Rd3), .en(1'b1), .Q(Rd4), .clk(Clk));  // open: clr
  Multiplexer #(.width(2), .enable("false")) multiplexer_25 (
    .in0(or_19_out), .in1(2'b00), .out(multiplexer_25_out), .sel(or_21_out));
  or or_21 (or_21_out, Branch, Stall);
  Multiplexer #(.select(2), .width(16), .enable("false")) multiplexer_26 (
    .in0(out_1), .in1(bit_extender_4_out), .in2(DataMemory_Out), .in3({J_12Im, Func, 4'b0000}),
    .out(DataForward), .sel(WBmem));
  Register #(.width(2)) WBexeCU (.D(multiplexer_25_out), .en(1'b1), .Q(WBexe), .clk(Clk));  // open: clr
  RAM #(.addrWidth(16), .dataWidth(16), .bus("separate")) ram_2 (
    .addr(out_1), .din(Rt_Out_Data), .data(DataMemory_Out), .str(SW), .clk(Clk), .ld(LW));  // open: sel, clr
  Register #(.width(2)) Rd2_9 (.D(MemExe), .en(1'b1), .Q({LW, SW}), .clk(Clk));  // open: clr
  Register #(.width(2)) Rd2_10 (.D(WBexe), .en(1'b1), .Q(WBmem), .clk(Clk));  // open: clr
  assign bit_extender_4_out = {{4{1'b0}}, NPCAlu};  // Bit_Extender bit_extender_4

  // Other names for the same wires on the sheet: J_12Im[2:0] = Func; Rt[2:0] = J_12Im[5:3]; Rs[2:0] = J_12Im[8:6];
  //   Rd[2:0] = J_12Im[11:9]; Alu_Out[15:0] = out_1; Branch_BR = Branch; Kill2 = Branch; MemExeLw = MemExe[1]

  // Notes on the sheet:
  //   Program Counter
  //   Instructions Memory
  //   I-Type
  //   R-type
  //   J-type
  //   Control Unit
  //   Register File
  //   SW
  //   LW
  //   BNE
  //   BEQ
  //   BGT
  //   BGE
  //   BLT
  //   BLE
  //   Load Upper Immediate
  //   Jump
  //   Jump and Link
  //   Arithmetic Logical Unit
  //   DataMemory
endmodule

module RegisterFile (
  input  [15:0] BusW,
  input  [2:0] RB,
  input  [2:0] RA,
  input  Clock,
  input  RegWrite,
  input  [2:0] RW,
  output [15:0] BusB,
  output [15:0] BusA
);

  wire _1_out, _2_out, _3_out, _4_out, _5_out, _6_out, _7_out, decoder_1_out1, decoder_1_out2,
       decoder_1_out3, decoder_1_out4, decoder_1_out5, decoder_1_out6, decoder_1_out7, decoder_2_out0,
       decoder_2_out1, decoder_2_out2, decoder_2_out3, decoder_2_out4, decoder_2_out5, decoder_2_out6,
       decoder_2_out7, decoder_3_out0, decoder_3_out1, decoder_3_out2, decoder_3_out3, decoder_3_out4,
       decoder_3_out5, decoder_3_out6, decoder_3_out7;
  wire [15:0] R1_q, R2_q, R3_q, R4_q, R5_q, R6_q, R7_q;

  Decoder #(.select(3)) decoder_1 (
    .out1(decoder_1_out1), .out2(decoder_1_out2), .out3(decoder_1_out3), .out4(decoder_1_out4),
    .out5(decoder_1_out5), .out6(decoder_1_out6), .out7(decoder_1_out7), .sel(RW), .en(1'b1));  // open: out0
  and _1 (_1_out, decoder_1_out1, RegWrite);
  and _2 (_2_out, decoder_1_out2, RegWrite);
  and _3 (_3_out, decoder_1_out3, RegWrite);
  and _4 (_4_out, decoder_1_out4, RegWrite);
  and _5 (_5_out, decoder_1_out5, RegWrite);
  and _6 (_6_out, decoder_1_out6, RegWrite);
  and _7 (_7_out, decoder_1_out7, RegWrite);
  Register #(.width(16)) R1 (.D(BusW), .en(_1_out), .Q(R1_q), .clk(Clock));  // open: clr
  Register #(.width(16)) R2 (.D(BusW), .en(_2_out), .Q(R2_q), .clk(Clock));  // open: clr
  Register #(.width(16)) R3 (.D(BusW), .en(_3_out), .Q(R3_q), .clk(Clock));  // open: clr
  Register #(.width(16)) R4 (.D(BusW), .en(_4_out), .Q(R4_q), .clk(Clock));  // open: clr
  Register #(.width(16)) R5 (.D(BusW), .en(_5_out), .Q(R5_q), .clk(Clock));  // open: clr
  Register #(.width(16)) R6 (.D(BusW), .en(_6_out), .Q(R6_q), .clk(Clock));  // open: clr
  Register #(.width(16)) R7 (.D(BusW), .en(_7_out), .Q(R7_q), .clk(Clock));  // open: clr
  assign BusA = decoder_2_out0 ? {16{1'b0}} : 16'bz;  // Controlled_Buffer controlled_buffer_1
  assign BusA = decoder_2_out2 ? R2_q : 16'bz;  // Controlled_Buffer controlled_buffer_2
  assign BusA = decoder_2_out1 ? R1_q : 16'bz;  // Controlled_Buffer controlled_buffer_3
  Decoder #(.select(3)) decoder_2 (
    .out0(decoder_2_out0), .out1(decoder_2_out1), .out2(decoder_2_out2), .out3(decoder_2_out3),
    .out4(decoder_2_out4), .out5(decoder_2_out5), .out6(decoder_2_out6), .out7(decoder_2_out7), .sel(RA),
    .en(1'b1));
  assign BusA = decoder_2_out6 ? R6_q : 16'bz;  // Controlled_Buffer controlled_buffer_4
  assign BusA = decoder_2_out5 ? R5_q : 16'bz;  // Controlled_Buffer controlled_buffer_5
  assign BusA = decoder_2_out4 ? R4_q : 16'bz;  // Controlled_Buffer controlled_buffer_6
  assign BusA = decoder_2_out3 ? R3_q : 16'bz;  // Controlled_Buffer controlled_buffer_7
  assign BusA = decoder_2_out7 ? R7_q : 16'bz;  // Controlled_Buffer controlled_buffer_8
  assign BusB = decoder_3_out0 ? {16{1'b0}} : 16'bz;  // Controlled_Buffer controlled_buffer_9
  assign BusB = decoder_3_out3 ? R3_q : 16'bz;  // Controlled_Buffer controlled_buffer_10
  assign BusB = decoder_3_out2 ? R2_q : 16'bz;  // Controlled_Buffer controlled_buffer_11
  assign BusB = decoder_3_out1 ? R1_q : 16'bz;  // Controlled_Buffer controlled_buffer_12
  Decoder #(.select(3)) decoder_3 (
    .out0(decoder_3_out0), .out1(decoder_3_out1), .out2(decoder_3_out2), .out3(decoder_3_out3),
    .out4(decoder_3_out4), .out5(decoder_3_out5), .out6(decoder_3_out6), .out7(decoder_3_out7), .sel(RB),
    .en(1'b1));
  assign BusB = decoder_3_out7 ? R7_q : 16'bz;  // Controlled_Buffer controlled_buffer_13
  assign BusB = decoder_3_out6 ? R6_q : 16'bz;  // Controlled_Buffer controlled_buffer_14
  assign BusB = decoder_3_out5 ? R5_q : 16'bz;  // Controlled_Buffer controlled_buffer_15
  assign BusB = decoder_3_out4 ? R4_q : 16'bz;  // Controlled_Buffer controlled_buffer_16

  // Notes on the sheet:
  //   STAGE 1
  //   STAGE 2
endmodule

module ALU (
  input  [3:0] Op,
  input  [2:0] func,
  input  [15:0] Rs,
  input  [15:0] Rt,
  output [15:0] Rd,
  output Zero
);

  wire comparator_1_eq, comparator_1_gt, comparator_1_lt, comparator_2_eq, comparator_2_gt, comparator_3_eq,
       comparator_3_gt, comparator_4_eq, comparator_4_gt, comparator_4_lt, not_1_out, or_2_out, or_3_out,
       or_4_out, or_5_out, or_6_out, or_7_out;
  wire [15:0] adder_1_out, adder_2_out, and_2_out, and_3_out, and_4_out, bit_extender_1_out,
       bit_extender_2_out, bit_extender_3_out, bit_extender_4_out, bit_extender_5_out, bit_extender_6_out,
       bit_extender_7_out, bit_extender_8_out, bit_extender_9_out, bit_extender_10_out, multiplexer_1_out,
       multiplexer_2_out, not_2_out, or_1_out, shifter_1_out, shifter_2_out, shifter_3_out, shifter_4_out,
       subtractor_1_out, xor_1_out;

  and and_1 (Zero, or_2_out, not_1_out);
  not not_1 (not_1_out, comparator_1_eq);
  Comparator #(.width(16), .mode("unsigned")) comparator_1 (
    .a(Rt), .b({16{1'b0}}), .gt(comparator_1_gt), .eq(comparator_1_eq), .lt(comparator_1_lt));
  assign or_1_out = Rs | Rt;  // OR_Gate or_1, 16 bits wide
  assign xor_1_out = Rt ^ Rs;  // XOR_Gate xor_1, 16 bits wide
  assign and_2_out = Rt & Rs;  // AND_Gate and_2, 16 bits wide
  Adder #(.width(16)) adder_1 (.a(Rs), .b(Rt), .out(adder_1_out));  // open: cin, cout
  Subtractor #(.width(16)) subtractor_1 (.a(Rs), .b(Rt), .out(subtractor_1_out));  // open: bin, bout
  Comparator #(.width(16)) comparator_2 (.a(Rs), .b(Rt), .gt(comparator_2_gt), .eq(comparator_2_eq));  // open: lt
  Comparator #(.width(16), .mode("unsigned")) comparator_3 (
    .a(Rs), .b(Rt), .gt(comparator_3_gt), .eq(comparator_3_eq));  // open: lt
  Shifter #(.width(16)) shifter_1 (.in(Rs), .\dist (Rt[3:0]), .out(shifter_1_out));
  Shifter #(.width(16), .shift("ar")) shifter_2 (.in(Rs), .\dist (Rt[3:0]), .out(shifter_2_out));
  assign bit_extender_1_out = {{15{comparator_1_eq}}, comparator_1_eq};  // Bit_Extender bit_extender_1
  or or_2 (or_2_out, comparator_1_gt, comparator_1_lt);
  assign not_2_out = ~and_2_out;  // NOT_Gate not_2, 16 bits wide
  or or_3 (or_3_out, comparator_2_gt, comparator_2_eq);
  or or_4 (or_4_out, comparator_3_gt, comparator_3_eq);
  Shifter #(.width(16), .shift("lr")) shifter_3 (.in(Rs), .\dist (Rt[3:0]), .out(shifter_3_out));
  Shifter #(.width(16), .shift("rr")) shifter_4 (.in(Rs), .\dist (Rt[3:0]), .out(shifter_4_out));
  assign and_3_out = bit_extender_1_out & Rs;  // AND_Gate and_3, 16 bits wide
  assign bit_extender_2_out = {{15{or_2_out}}, or_2_out};  // Bit_Extender bit_extender_2
  assign and_4_out = bit_extender_2_out & Rs;  // AND_Gate and_4, 16 bits wide
  assign bit_extender_3_out = {{15{1'b0}}, or_3_out};  // Bit_Extender bit_extender_3
  assign bit_extender_4_out = {{15{1'b0}}, or_4_out};  // Bit_Extender bit_extender_4
  Comparator #(.width(16)) comparator_4 (
    .a(Rt), .b(Rs), .gt(comparator_4_gt), .eq(comparator_4_eq), .lt(comparator_4_lt));
  Multiplexer #(.select(3), .width(16), .enable("false")) multiplexer_1 (
    .in0(or_1_out), .in1(and_2_out), .in2(not_2_out), .in3(xor_1_out), .in4(adder_1_out),
    .in5(subtractor_1_out), .in6(bit_extender_3_out), .in7(bit_extender_4_out), .out(multiplexer_1_out),
    .sel(func));
  Multiplexer #(.select(3), .width(16), .enable("false")) multiplexer_2 (
    .in0(shifter_1_out), .in1(shifter_3_out), .in2(shifter_2_out), .in3(shifter_4_out), .in4(and_3_out),
    .in5(and_4_out), .in6({16{1'b0}}), .in7({16{1'b0}}), .out(multiplexer_2_out), .sel(func));
  assign bit_extender_5_out = {{15{1'b0}}, comparator_4_eq};  // Bit_Extender bit_extender_5
  or or_5 (or_5_out, comparator_4_gt, comparator_4_lt);
  assign bit_extender_6_out = {{15{1'b0}}, or_5_out};  // Bit_Extender bit_extender_6
  assign bit_extender_7_out = {{15{1'b0}}, comparator_4_gt};  // Bit_Extender bit_extender_7
  assign bit_extender_8_out = {{15{1'b0}}, or_6_out};  // Bit_Extender bit_extender_8
  or or_6 (or_6_out, comparator_4_gt, comparator_4_eq);
  assign bit_extender_9_out = {{15{1'b0}}, comparator_4_lt};  // Bit_Extender bit_extender_9
  or or_7 (or_7_out, comparator_4_eq, comparator_4_lt);
  assign bit_extender_10_out = {{15{1'b0}}, or_7_out};  // Bit_Extender bit_extender_10
  Adder #(.width(16)) adder_2 (.a(Rs), .b(Rt), .out(adder_2_out));  // open: cin, cout
  Multiplexer #(.select(4), .width(16), .enable("false")) multiplexer_3 (
    .in0(multiplexer_1_out), .in1(multiplexer_2_out), .in2(and_2_out), .in3(or_1_out), .in4(adder_1_out),
    .in5(adder_2_out), .in6(adder_2_out), .in7(bit_extender_6_out), .in8(bit_extender_5_out),
    .in9(bit_extender_7_out), .in10(bit_extender_8_out), .in11(bit_extender_9_out),
    .in12(bit_extender_10_out), .in13({16{1'b0}}), .in14({16{1'b0}}), .in15({16{1'b0}}), .out(Rd), .sel(Op));

  // Notes on the sheet:
  //   ALU For Op = 0001
  //   SLL
  //   SRL
  //   SRA
  //   ROR
  //   MOVZ MOVN
  //   ALU For Op = 0000
  //   OR 
  //   NAND
  //   XOR
  //   ADD
  //   SUB
  //   SGE
  //   SGEU
  //   Signed
  //   Signed
endmodule
